# Fritzing sketch sweet dispenser3 (saved by Fritzing 0.7.7b)
breadboards: 1

parts:
  Arduino1 = Arduino
  LED1 = LED - 5mm [color="Green (570nm)" package="5 mm [THT]"]
  R2 = Resistor [tolerance=±5% resistance=100k package=THT]
  R4 = Resistor [tolerance=±5% resistance=470 package=THT]
  J4 = male pin header, 3 pins [form="♂ (male)"]
  S2 = Pushbutton [package="[THT]"]
  R6 = Rotary Potentiometer (Large) [maximum_resistance=100kΩ package=THT]
  J5 = Basic Servo

nets:
  N1: Arduino1.D9, R4.Pin_0
  N2: Arduino1.D5, J4.pin3, J5.pulse
  N3: Arduino1.D4, R2.Pin_0, S2.Pin_3, S2.Pin_4
  +5V: Arduino1.+5V, J4.pin2, S2.Pin_1, S2.Pin_2, R6.leg2, J5.vcc
  GND: Arduino1.GND, LED1.cathode, R2.Pin_1, J4.pin1, R6.leg1, J5.gnd
  N4: Arduino1.A0, R6.wiper
  N5: LED1.anode, R4.Pin_1
